# Fritzing sketch Breadboard Sketch (saved by Fritzing 0.9.3b)
breadboards: 2

parts:
  Part1 = Arduino Uno (Rev3)
  U1 = 74HC595 [package="DIP16 [THT]"]
  U2 = 74HC595 [package="DIP16 [THT]"]
  Disp1 = LBT2088AH [part_number=LBT2088AH]

nets:
  N1: Part1.D8, U1.ST_CP
  N2: Part1.D10_PWM/SS, U1.SH_CP
  N3: Part1.D11_PWM/MOSI, U1.DS
  VCC: Part1.5V, U1.MR, U1.VCC, U2.MR, U2.VCC
  GND: Part1.GND, U1.GND, U1.OE, U2.GND, U2.OE
  N4: U1.Q1, Disp1.pin2
  N5: U1.Q2, Disp1.pin_3
  N6: U1.Q3, Disp1.pin_4
  N7: U1.Q4, Disp1.pin_16
  N8: U1.Q5, Disp1.pin_15
  N9: U1.Q6, Disp1.pin_14
  N10: U1.Q7, Disp1.pin_13
  N11: U1.Q7', U2.DS
  N12: U1.Q0, Disp1.pin1
  N13: U2.Q1, Disp1.pin_7
  N14: U2.Q2, Disp1.pin_6
  N15: U2.Q3, Disp1.pin_5
  N16: U2.Q4, Disp1.pin_9
  N17: U2.Q5, Disp1.pin_10
  N18: U2.Q6, Disp1.pin_11
  N19: U2.Q7, Disp1.pin_12
  N20: U2.Q0, Disp1.pin_8

notes:
  Luckylight LED Matrix text on this side
